# Fritzing sketch sketch (saved by Fritzing 0.9.3b)

parts:
  Componente1 = Arduino Uno (Rev3)
  S1 = H-Bridge with L298N
  M1 = DC Motor
  M2 = DC Motor
  VCC1 = Battery
  J1 = Basic Servo
  J2 = Basic Servo
  hc-sr1 = hc-sr04
  Componente2 = Bluetooth HC-05 Macho

nets:
  N1: Componente1.A0, J1.pulse
  N2: Componente1.A1, J2.pulse
  N3: Componente1.D9_PWM, S1.ENA
  N4: Componente1.D12/MISO, hc-sr1.Echo
  N5: Componente1.D13/SCK, hc-sr1.Trig
  GND: Componente1.GND, S1.GND, VCC1.-, J1.gnd, J2.gnd, hc-sr1.GND, Componente2.GND
  N6: Componente1.D0/RX, Componente2.TXD
  N7: Componente1.D1/TX, Componente2.RXD
  N8: Componente1.D2, S1.IN4
  N9: Componente1.D3_PWM, S1.IN3
  N10: Componente1.D4, S1.IN2
  N11: Componente1.D5_PWM, S1.IN1
  N12: Componente1.D6_PWM, S1.ENB
  3V3: Componente1.3V3, Componente2.VCC
  VCC: Componente1.5V, J1.vcc, J2.vcc, hc-sr1.VCC
  VIN: Componente1.VIN, S1.5V
  N13: S1.12V, VCC1.+
  N14: S1.M1-01, M2.pin_2
  N15: S1.M1-02, M2.pin_1
  N16: S1.M2-01, M1.pin_2
  N17: S1.M2-02, M1.pin_1

custom parts:
  H-Bridge with L298N: h-bridge

// code stored in the sketch: main.ino
#include "./motors/motors.h"
#include "./sensors/sensors.h"


// Variables
int time = 0;
char junk;
String inputString = "";


Motors controler({5, 4, 3, 2, 6, 9, A0, A1});
Sensors sensors({12, 13});


void setup() {
    Serial.begin(9600);
};
void loop() {
    if (Serial.available()) {
        while (Serial.available()) {
            inputString += (char)Serial.read();
        };
        Serial.println(inputString);
        while (Serial.available() > 0 ) {
            junk = Serial.read();
        };
        if (inputString == "F") { controler.front(); }
        else if (inputString == "B") { controler.back(); }
        else if (inputString == "L") { controler.left(); }
        else if (inputString == "R") { controler.right(); }
        inputString = "";
    }
    if (time % 20 == 0) { controler.update(); };
    if (time % 50 == 0) { sensors.update(); };
    time += 1;
};
