# Fritzing sketch sketch (saved by Fritzing 0.9.3b)

parts:
  Componente1 = Arduino Uno (Rev3)
  S1 = H-Bridge with L298N
  M1 = DC Motor
  M2 = DC Motor
  VCC1 = Battery
  J1 = Basic Servo
  J2 = Basic Servo

nets:
  N1: Componente1.A0, J1.pulse
  N2: Componente1.A1, J2.pulse
  N3: Componente1.D9_PWM, S1.ENA
  N4: Componente1.D2, S1.IN4
  N5: Componente1.D3_PWM, S1.IN3
  N6: Componente1.D4, S1.IN2
  N7: Componente1.D5_PWM, S1.IN1
  N8: Componente1.D6_PWM, S1.ENB
  VCC: Componente1.5V, J1.vcc, J2.vcc
  GND: Componente1.GND, S1.GND, VCC1.-, J1.gnd, J2.gnd
  VIN: Componente1.VIN, S1.5V
  N9: S1.12V, VCC1.+
  N10: S1.M1-01, M2.pin_2
  N11: S1.M1-02, M2.pin_1
  N12: S1.M2-01, M1.pin_2
  N13: S1.M2-02, M1.pin_1

custom parts:
  H-Bridge with L298N: h-bridge

// code stored in the sketch: main.ino
#include "motors.h"

void setup() {
    Motors controler(5, 4, 3, 2, 6, 9, A0, A1);
    // in1, in2, in3, in4, enA, enB, servo1, servo2 
};
void loop() {
    controler.update();
    delay(100);
};
